# Fritzing sketch LCDThermometre (saved by Fritzing 0.9.4)
breadboards: 1

parts:
  Parça1 = Arduino Uno (Rev3)
  Parça2 = LCD1602-I2C
  S1 = Round Pushbutton
  R1 = Resistor [tolerance=±5% resistance=10k package=THT]
  DHT1 = DHT11 Humitidy and Temperature Sensor

nets:
  N1: Parça1.A4/SDA, Parça2.SDA
  N2: Parça1.A5/SCL, Parça2.SCL
  N3: Parça1.D2, DHT1.DATA
  N4: Parça1.D4, S1.leg0
  5V: Parça1.5V, Parça2.VCC, DHT1.VDD
  GND: Parça1.GND, Parça2.GND, S1.leg1, R1.Pin_0, R1.Pin_1, DHT1.GND

custom parts:
  LCD1602-I2C: A standard character display, usually with 2x16 characters. Comes in many colors with LCM1602 IIC attached.
  DHT11 Humitidy and Temperature Sensor: DHT11 Humidity and Temperature Sensor
